// Logisim project LOTP_8-Bit-CPU-V4-7400.circ as structural Verilog: 3 circuits, main circuit main
module main (
);

  wire clock_1_out, dip_7474_1_p7, dip_7474_1_p12, dip_7474_1_p13, dip_7474_1_p17, dip_7474_2_p1,
       dip_7474_2_p3, dip_7474_2_p5, dip_7474_2_p7, dip_7474_2_p12, dip_7474_2_p13, dip_7474_2_p17,
       dip_74173_1_q0, dip_74173_1_q1, dip_74173_1_q2, dip_74173_1_q3, dip_74245_1_a1_2, dip_74245_1_a2_2,
       dip_74245_1_a3_2, dip_74245_1_a4_2, dip_74245_1_a5_2, dip_74245_1_a6_2, dip_74245_1_a7_2,
       dip_74245_1_a8_2, dip_74245_1_b1_2, dip_74245_1_b2_2, dip_74245_1_b3_2, dip_74245_1_b4_2,
       dip_74245_1_b5_2, dip_74245_1_b6_2, dip_74245_1_b7_2, dip_74245_1_b8_2, dip_74573_2_p2,
       dip_74573_2_p4, dip_74573_2_p6, dip_74573_2_p8, dip_74573_2_p10, R_AREG, RESET, W_AREG, W_BREG,
       W_CALREG;

  DIP_74245 dip_74245_1 (
    .DIR(1'b0), .B1_2(dip_74245_1_b1_2), .B1(dip_74245_1_b1_2), .A1(dip_74245_1_a1_2),
    .A1_2(dip_74245_1_a1_2), .B2_2(dip_74245_1_b2_2), .B2(dip_74245_1_b2_2), .A2(dip_74245_1_a2_2),
    .A2_2(dip_74245_1_a2_2), .B3_2(dip_74245_1_b3_2), .B3(dip_74245_1_b3_2), .A3(dip_74245_1_a3_2),
    .A3_2(dip_74245_1_a3_2), .B4_2(dip_74245_1_b4_2), .B4(dip_74245_1_b4_2), .A4(dip_74245_1_a4_2),
    .A4_2(dip_74245_1_a4_2), .B5_2(dip_74245_1_b5_2), .B5(dip_74245_1_b5_2), .B6_2(dip_74245_1_b6_2),
    .B6(dip_74245_1_b6_2), .A5(dip_74245_1_a5_2), .A5_2(dip_74245_1_a5_2), .A6(dip_74245_1_a6_2),
    .A6_2(dip_74245_1_a6_2), .B7_2(dip_74245_1_b7_2), .B7(dip_74245_1_b7_2), .B8_2(dip_74245_1_b8_2),
    .B8(dip_74245_1_b8_2), .A7(dip_74245_1_a7_2), .A7_2(dip_74245_1_a7_2), .A8(dip_74245_1_a8_2),
    .A8_2(dip_74245_1_a8_2), .EN_prime(R_AREG));
  DIP_74173 dip_74173_1 (
    .IE1_prime(W_CALREG), .IE2_prime(W_CALREG), .CP(clock_1_out), .MR(RESET), .OE1_prime(1'b0),
    .OE2_prime(1'b0), .D0(dip_74245_1_a5_2), .D1(dip_74245_1_a6_2), .D2(dip_74245_1_a7_2),
    .D3(dip_74245_1_a8_2), .Q0(dip_74173_1_q0), .Q1(dip_74173_1_q1), .Q2(dip_74173_1_q2), .Q3(dip_74173_1_q3));
  DotMatrix #(.matrixcols(8), .matrixrows(1)) dotmatrix_1 (
    .col0(dip_74245_1_b1_2), .col1(dip_74245_1_b2_2), .col2(dip_74245_1_b3_2), .col3(dip_74245_1_b4_2),
    .col4(dip_74245_1_b5_2), .col5(dip_74245_1_b6_2), .col6(dip_74245_1_b7_2), .col7(dip_74245_1_b8_2));
  Pull_Resistor #(.pull(1)) pull_resistor_1 (.node(R_AREG));
  Pull_Resistor #(.pull(1)) pull_resistor_2 (.node(W_CALREG));
  Clock clock_1 (.out(clock_1_out));
  DotMatrix #(.matrixcols(8), .matrixrows(1)) dotmatrix_2 (
    .col0(dip_74573_2_p2), .col1(dip_74573_2_p4), .col2(dip_74573_2_p6), .col3(dip_74573_2_p8),
    .col4(dip_74573_2_p10), .col5(dip_7474_2_p1), .col6(dip_7474_2_p3), .col7(dip_7474_2_p5));
  Button button_1 (.out(RESET));
  // DIP_74573 dip_74573_1: pin names not known; wires that end beside it: 1'b0, dip_74245_1_b1_2, dip_74245_1_a1_2, dip_74245_1_b2_2, dip_74245_1_a2_2, dip_74245_1_b3_2, dip_74245_1_a3_2, dip_74245_1_b4_2, dip_74245_1_a4_2, dip_74245_1_b5_2, dip_74245_1_a5_2
  // DIP_74573 dip_74573_2: pin names not known; wires that end beside it: 1'b0, dip_74573_2_p2, dip_74245_1_a1_2, dip_74573_2_p4, dip_74245_1_a2_2, dip_74573_2_p6, dip_74245_1_a3_2, dip_74573_2_p8, dip_74245_1_a4_2, dip_74573_2_p10, dip_74245_1_a5_2
  // DIP_7474 dip_7474_1: pin names not known; wires that end beside it: dip_74245_1_b6_2, dip_74245_1_a6_2, dip_74245_1_b7_2, dip_74245_1_a7_2, dip_74245_1_b8_2, dip_74245_1_a8_2, dip_7474_1_p7, RESET, RESET, W_AREG, 1'b1, dip_7474_1_p12, dip_7474_1_p13, 1'b1, dip_7474_1_p12, dip_7474_1_p13, dip_7474_1_p17
  Pull_Resistor pull_resistor_3 (.node(W_AREG));
  // DIP_74283 dip_74283_1: pin names not known; wires that end beside it: dip_74173_1_q0, dip_74173_1_q1, dip_74173_1_q2, dip_74173_1_q3
  DIP_74245 dip_74245_2 ();  // open: DIR, B1_2, B1, A1, A1_2, B2_2, B2, A2, A2_2, B3_2, B3, A3, A3_2, B4_2, B4, A4, A4_2, B5_2, B5, B6_2, B6, A5, A5_2, A6, A6_2, B7_2, B7, B8_2, B8, A7, A7_2, A8, A8_2, EN_prime
  // DIP_7474 dip_7474_2: pin names not known; wires that end beside it: dip_7474_2_p1, dip_74245_1_a6_2, dip_7474_2_p3, dip_74245_1_a7_2, dip_7474_2_p5, dip_74245_1_a8_2, dip_7474_2_p7, RESET, RESET, W_BREG, 1'b1, dip_7474_2_p12, dip_7474_2_p13, 1'b1, dip_7474_2_p12, dip_7474_2_p13, dip_7474_2_p17
  Pull_Resistor pull_resistor_4 (.node(W_BREG));
  Clock clock_2 (.out(dip_7474_1_p12));
  // DIP_7408 dip_7408_1: pin names not known
  // DIP_74283 dip_74283_2: pin names not known
  Clock clock_3 (.out(dip_7474_2_p12));
  Transistor #(.\type ("n")) transistor_1 (.out(dip_7474_1_p7), .gate(dip_7474_1_p13));  // open: in
  Transistor #(.\type ("n")) transistor_2 (.in(1'b0), .gate(dip_7474_1_p17));  // open: out
  Pull_Resistor #(.pull(1)) pull_resistor_5 (.node(dip_7474_1_p7));
  // DIP_7408 dip_7408_2: pin names not known
  Transistor #(.\type ("n")) transistor_3 (.out(dip_7474_2_p7), .gate(dip_7474_2_p13));  // open: in
  Transistor #(.\type ("n")) transistor_4 (.in(1'b0), .gate(dip_7474_2_p17));  // open: out
  Pull_Resistor #(.pull(1)) pull_resistor_6 (.node(dip_7474_2_p7));
  // DIP_74139 dip_74139_1: pin names not known
  // DIP_7486 dip_7486_1: pin names not known
  DIP_74245 dip_74245_3 ();  // open: DIR, B1_2, B1, A1, A1_2, B2_2, B2, A2, A2_2, B3_2, B3, A3, A3_2, B4_2, B4, A4, A4_2, B5_2, B5, B6_2, B6, A5, A5_2, A6, A6_2, B7_2, B7, B8_2, B8, A7, A7_2, A8, A8_2, EN_prime
  // DIP_7486 dip_7486_2: pin names not known
  // DIP_7486 dip_7486_3: pin names not known
  DIP_74245 dip_74245_4 ();  // open: DIR, B1_2, B1, A1, A1_2, B2_2, B2, A2, A2_2, B3_2, B3, A3, A3_2, B4_2, B4, A4, A4_2, B5_2, B5, B6_2, B6, A5, A5_2, A6, A6_2, B7_2, B7, B8_2, B8, A7, A7_2, A8, A8_2, EN_prime
  // DIP_7432 dip_7432_1: pin names not known
  DIP_74245 dip_74245_5 ();  // open: DIR, B1_2, B1, A1, A1_2, B2_2, B2, A2, A2_2, B3_2, B3, A3, A3_2, B4_2, B4, A4, A4_2, B5_2, B5, B6_2, B6, A5, A5_2, A6, A6_2, B7_2, B7, B8_2, B8, A7, A7_2, A8, A8_2, EN_prime
  // DIP_7486 dip_7486_4: pin names not known
  DIP_74245 dip_74245_6 ();  // open: DIR, B1_2, B1, A1, A1_2, B2_2, B2, A2, A2_2, B3_2, B3, A3, A3_2, B4_2, B4, A4, A4_2, B5_2, B5, B6_2, B6, A5, A5_2, A6, A6_2, B7_2, B7, B8_2, B8, A7, A7_2, A8, A8_2, EN_prime
  // DIP_7432 dip_7432_2: pin names not known
  // DIP_7408 dip_7408_3: pin names not known
  // DIP_7402 dip_7402_1: pin names not known
  // DIP_7408 dip_7408_4: pin names not known
  DIP_74245 dip_74245_7 ();  // open: DIR, B1_2, B1, A1, A1_2, B2_2, B2, A2, A2_2, B3_2, B3, A3, A3_2, B4_2, B4, A4, A4_2, B5_2, B5, B6_2, B6, A5, A5_2, A6, A6_2, B7_2, B7, B8_2, B8, A7, A7_2, A8, A8_2, EN_prime
  // DIP_7402 dip_7402_2: pin names not known
  DIP_74245 dip_74245_8 ();  // open: DIR, B1_2, B1, A1, A1_2, B2_2, B2, A2, A2_2, B3_2, B3, A3, A3_2, B4_2, B4, A4, A4_2, B5_2, B5, B6_2, B6, A5, A5_2, A6, A6_2, B7_2, B7, B8_2, B8, A7, A7_2, A8, A8_2, EN_prime

  // Notes on the sheet:
  //   A Register
  //   Calculation Register
  //   B Register
  //   74173
  //   74245
endmodule

module DIP_74245 (
  input  EN_prime,
  input  B1,
  input  B2,
  input  B3,
  input  B4,
  input  B5,
  input  B6,
  input  B7,
  input  B8,
  input  A1,
  input  A2,
  input  A3,
  input  A4,
  input  A5,
  input  A6,
  input  A7,
  input  A8,
  input  DIR,
  output B1_2,
  output B2_2,
  output B3_2,
  output B4_2,
  output B5_2,
  output B6_2,
  output B7_2,
  output B8_2,
  output A1_2,
  output A2_2,
  output A3_2,
  output A4_2,
  output A5_2,
  output A6_2,
  output A7_2,
  output A8_2
);

  wire and_1_out, and_2_out, not_1_out, not_2_out, not_3_out;

  not not_1 (not_1_out, EN_prime);
  not not_2 (not_2_out, DIR);
  and and_1 (and_1_out, not_2_out, not_1_out);
  assign B1_2 = and_2_out ? A1 : 1'bz;  // Controlled_Buffer controlled_buffer_1
  and and_2 (and_2_out, DIR, not_3_out);
  not not_3 (not_3_out, EN_prime);
  assign A2_2 = and_1_out ? B2 : 1'bz;  // Controlled_Buffer controlled_buffer_2
  assign A1_2 = and_1_out ? B1 : 1'bz;  // Controlled_Buffer controlled_buffer_3
  assign B2_2 = and_2_out ? A2 : 1'bz;  // Controlled_Buffer controlled_buffer_4
  assign B3_2 = and_2_out ? A3 : 1'bz;  // Controlled_Buffer controlled_buffer_5
  assign A4_2 = and_1_out ? B4 : 1'bz;  // Controlled_Buffer controlled_buffer_6
  assign A3_2 = and_1_out ? B3 : 1'bz;  // Controlled_Buffer controlled_buffer_7
  assign B5_2 = and_2_out ? A5 : 1'bz;  // Controlled_Buffer controlled_buffer_8
  assign B4_2 = and_2_out ? A4 : 1'bz;  // Controlled_Buffer controlled_buffer_9
  assign A5_2 = and_1_out ? B5 : 1'bz;  // Controlled_Buffer controlled_buffer_10
  assign A6_2 = and_1_out ? B6 : 1'bz;  // Controlled_Buffer controlled_buffer_11
  assign B6_2 = and_2_out ? A6 : 1'bz;  // Controlled_Buffer controlled_buffer_12
  assign B7_2 = and_2_out ? A7 : 1'bz;  // Controlled_Buffer controlled_buffer_13
  assign A8_2 = and_1_out ? B8 : 1'bz;  // Controlled_Buffer controlled_buffer_14
  assign A7_2 = and_1_out ? B7 : 1'bz;  // Controlled_Buffer controlled_buffer_15
  assign B8_2 = and_2_out ? A8 : 1'bz;  // Controlled_Buffer controlled_buffer_16
endmodule

module DIP_74173 (
  input  D0,
  input  D1,
  input  D2,
  input  D3,
  input  IE1_prime,
  input  IE2_prime,
  input  CP,
  input  MR,
  input  OE1_prime,
  input  OE2_prime,
  output Q0,
  output Q1,
  output Q2,
  output Q3
);

  wire and_1_out, and_2_out, and_3_out, and_4_out, and_5_out, and_6_out, and_7_out, and_8_out, and_9_out,
       and_10_out, d_ff_1_q, d_ff_1_qn, d_ff_2_q, d_ff_2_qn, d_ff_3_q, d_ff_3_qn, d_ff_4_q, d_ff_4_qn,
       not_1_out, not_2_out, not_3_out, not_4_out, not_5_out, or_1_out, or_2_out, or_3_out, or_4_out;

  not not_1 (not_1_out, IE1_prime);
  not not_2 (not_2_out, IE2_prime);
  not not_3 (not_3_out, OE1_prime);
  not not_4 (not_4_out, OE2_prime);
  and and_1 (and_1_out, not_1_out, not_2_out);
  not not_5 (not_5_out, and_1_out);
  and and_2 (and_2_out, not_3_out, not_4_out);
  and and_3 (and_3_out, D0, and_1_out);
  and and_4 (and_4_out, not_5_out, d_ff_1_q);
  or or_1 (or_1_out, and_3_out, and_4_out);
  D_Flip_Flop d_ff_1 (.clk(CP), .D(or_1_out), .Q(d_ff_1_q), .Qn(d_ff_1_qn), .preset(1'b0), .en(1'b1), .reset(MR));
  assign Q0 = and_2_out ? ~d_ff_1_qn : 1'bz;  // Controlled_Inverter controlled_inverter_1
  and and_5 (and_5_out, not_5_out, d_ff_2_q);
  and and_6 (and_6_out, D1, and_1_out);
  or or_2 (or_2_out, and_6_out, and_5_out);
  D_Flip_Flop d_ff_2 (.clk(CP), .D(or_2_out), .Q(d_ff_2_q), .Qn(d_ff_2_qn), .preset(1'b0), .en(1'b1), .reset(MR));
  and and_7 (and_7_out, D2, and_1_out);
  or or_3 (or_3_out, and_7_out, and_8_out);
  assign Q1 = and_2_out ? ~d_ff_2_qn : 1'bz;  // Controlled_Inverter controlled_inverter_2
  and and_8 (and_8_out, not_5_out, d_ff_3_q);
  and and_9 (and_9_out, D3, and_1_out);
  D_Flip_Flop d_ff_3 (.clk(CP), .D(or_3_out), .Q(d_ff_3_q), .Qn(d_ff_3_qn), .preset(1'b0), .en(1'b1), .reset(MR));
  assign Q2 = and_2_out ? ~d_ff_3_qn : 1'bz;  // Controlled_Inverter controlled_inverter_3
  and and_10 (and_10_out, not_5_out, d_ff_4_q);
  or or_4 (or_4_out, and_9_out, and_10_out);
  D_Flip_Flop d_ff_4 (.clk(CP), .D(or_4_out), .Q(d_ff_4_q), .Qn(d_ff_4_qn), .preset(1'b0), .en(1'b1), .reset(MR));
  assign Q3 = and_2_out ? ~d_ff_4_qn : 1'bz;  // Controlled_Inverter controlled_inverter_4
endmodule
