// Logisim project LOTP_8-Bit-CPU-V4.circ as structural Verilog: 2 circuits, main circuit west
module west (
  input  [7:0] in_1,
  input  in_2
);

  wire and_1_out, button_1_out, CLK, clock_1_out, counter_1_carry, Counter_Up, HALT, nor_1_out, nor_2_out,
       nor_3_out, not_1_out, not_2_out, not_3_out, or_1_out, or_2_out, OUTPUT_SET, Overflow, R_ALU, R_AREG,
       R_Counter, R_INPUT, R_IREG, R_PrgEEPROM, R_STKMEM, Reset_Microcode, RST, StackDown, StackUp, START,
       STOP, W_ADR_REG, W_AREG, W_BREG, W_CALREG, W_Counter, W_IREG, W_PrgEEPROM, W_STKMEM, Zero;
  wire [3:0] counter_1_q, register_3_q;
  wire [7:0] alu_1_c, BUS, controlled_buffer_8_out, counter_2_q, counter_3_q, OUTPUT, ram_1_data,
       register_1_q, register_2_q, register_5_q, register_6_q, rom_1_data;
  wire [7:5] rom_2_data;

  assign BUS = R_IREG ? register_2_q : 8'bz;  // Controlled_Buffer controlled_buffer_1
  Counter #(.width(4), .max('hf)) counter_1 (
    .load(Reset_Microcode), .D(4'b0000), .count(not_1_out), .Q(counter_1_q), .carry(counter_1_carry),
    .clk(not_2_out), .clr(RST));
  not not_1 (not_1_out, Reset_Microcode);
  not not_2 (not_2_out, CLK);
  Register register_1 (.D(BUS), .en(W_ADR_REG), .Q(register_1_q), .clk(CLK), .clr(RST));
  Register register_2 (.D(BUS), .en(W_IREG), .Q(register_2_q), .clk(CLK), .clr(RST));
  Decoder #(.select(4), .disabled(0), .enable("false")) decoder_1 (
    .out1(R_Counter), .out2(R_PrgEEPROM), .out3(R_IREG), .out4(R_AREG), .out5(R_INPUT), .out6(R_STKMEM),
    .out7(R_ALU), .sel(rom_1_data[3:0]));  // open: out0, out8, out9, out10, out11, out12, out13, out14, out15
  ROM #(.addrWidth(11)) rom_1 (
    .addr({in_2, Overflow, Zero, register_2_q[3:0], counter_1_q}), .data(rom_1_data));  // open: sel
  ROM #(.addrWidth(11)) rom_2 (
    .addr({in_2, Overflow, Zero, register_2_q[3:0], counter_1_q}),
    .data({rom_2_data, Reset_Microcode, StackDown, StackUp, Counter_Up, HALT}));  // open: sel
  or or_1 (or_1_out, Counter_Up, counter_1_carry);
  Counter counter_2 (
    .load(W_Counter), .D(BUS), .count(or_1_out), .Q(counter_2_q), .clk(CLK), .clr(RST));  // open: carry
  RAM ram_1 (.addr(register_1_q), .data(ram_1_data), .clk(CLK), .ld(not_3_out), .clr(button_1_out));  // open: sel
  not not_3 (not_3_out, W_PrgEEPROM);
  Button button_1 (.out(button_1_out));
  assign BUS = R_Counter ? counter_2_q : 8'bz;  // Controlled_Buffer controlled_buffer_2
  assign ram_1_data = W_PrgEEPROM ? BUS : 8'bz;  // Controlled_Buffer controlled_buffer_3
  assign BUS = R_PrgEEPROM ? ram_1_data : 8'bz;  // Controlled_Buffer controlled_buffer_4
  Decoder #(.select(4), .disabled(0), .enable("false")) decoder_2 (
    .out1(W_Counter), .out2(W_ADR_REG), .out3(W_PrgEEPROM), .out4(W_IREG), .out5(W_AREG), .out6(W_BREG),
    .out7(W_CALREG), .out8(OUTPUT_SET), .out9(W_STKMEM), .sel(rom_1_data[7:4]));  // open: out0, out10, out11, out12, out13, out14, out15
  or or_2 (or_2_out, RST, STOP, and_1_out);
  and and_1 (and_1_out, HALT, CLK);
  Clock clock_1 (.out(clock_1_out));
  nor nor_1 (nor_1_out, or_2_out, nor_2_out);
  nor nor_2 (nor_2_out, nor_1_out, START);
  assign BUS = R_INPUT ? in_1 : 8'bz;  // Controlled_Buffer controlled_buffer_5
  and and_2 (CLK, clock_1_out, nor_1_out);
  assign BUS = R_AREG ? register_5_q : 8'bz;  // Controlled_Buffer controlled_buffer_6
  Register #(.width(4)) register_3 (.D(BUS[7:4]), .en(W_CALREG), .Q(register_3_q), .clk(CLK), .clr(RST));
  assign BUS = R_ALU ? alu_1_c : 8'bz;  // Controlled_Buffer controlled_buffer_7
  nor nor_3 (nor_3_out, StackUp, StackDown);
  Counter counter_3 (.load(nor_3_out), .count(StackUp), .Q(counter_3_q), .clk(CLK), .clr(RST));  // open: D, carry
  Register register_4 (.D(BUS), .en(OUTPUT_SET), .Q(OUTPUT), .clk(CLK), .clr(RST));
  Register register_5 (.D(BUS), .en(W_AREG), .Q(register_5_q), .clk(CLK), .clr(RST));
  ALU alu_1 (.CAL(register_3_q), .A(register_5_q), .C(alu_1_c), .Zero(Zero), .Overflow(Overflow), .B(register_6_q));
  Register register_6 (.D(BUS), .en(W_BREG), .Q(register_6_q), .clk(CLK), .clr(RST));
  Button button_2 (.out(RST));
  Button button_3 (.out(STOP));
  Button button_4 (.out(START));
  assign controlled_buffer_8_out = W_STKMEM ? BUS : 8'bz;  // Controlled_Buffer controlled_buffer_8
  RAM ram_2 (.addr(counter_3_q), .data(controlled_buffer_8_out), .clk(CLK), .ld(R_STKMEM), .clr(RST));  // open: sel
  assign BUS = R_STKMEM ? controlled_buffer_8_out : 8'bz;  // Controlled_Buffer controlled_buffer_9
  LED led_1 (.in(R_Counter));
  LED led_2 (.in(R_PrgEEPROM));
  LED led_3 (.in(R_IREG));
  LED led_4 (.in(R_AREG));
  LED led_5 (.in(R_INPUT));
  LED led_6 (.in(R_STKMEM));
  LED led_7 (.in(R_ALU));
  LED led_8 (.in(W_Counter));
  LED led_9 (.in(W_ADR_REG));
  LED led_10 (.in(W_PrgEEPROM));
  LED led_11 (.in(W_IREG));
  LED led_12 (.in(W_AREG));
  LED led_13 (.in(W_BREG));
  LED led_14 (.in(W_CALREG));
  LED led_15 (.in(OUTPUT_SET));
  LED led_16 (.in(W_STKMEM));
  LED led_17 (.in(HALT));
  LED led_18 (.in(Counter_Up));
  LED led_19 (.in(StackUp));
  LED led_20 (.in(StackDown));
  LED led_21 (.in(Reset_Microcode));
  LED led_22 (.in(CLK));
  // Probe on BUS
  // Probe on BUS
  // Probe on BUS
  // Probe on OUTPUT
  // Probe on OUTPUT
  // Probe on OUTPUT
  LED led_23 (.in(OUTPUT_SET));

  // Other names for the same wires on the sheet: BOOTLOADER = in_2; INPUT[7:0] = in_1; W_OUT = OUTPUT_SET

  // Notes on the sheet:
  //   Instruction
  //   Register
  //   Microcode EEPROM A
  //   Microcode EEPROM B
  //   Read 
  //   contents of rom_1 (hex, n*v repeats v):
  //   21 42 14*0 21 42 21 52 12*0 21 42 21 22 52 11*0 21 42 21 22 34 11*0 21 42 21 62 12*0 21 42 73 13*0
  //   21 42 57 13*0 21 42 21 12 12*0 21 42 14*0 21 42 14*0 21 42 94 13*0 21 42 0 56 12*0 21 42 55 13*0 21
  //   42 84 13*0 21 42 14*0 21 42 14*0 21 42 14*0 21 42 21 52 12*0 21 42 21 22 52 11*0 21 42 21 22 34 11*0
  //   21 42 21 62 12*0 21 42 73 13*0 21 42 57 13*0 21 42 21 12 12*0 21 42 21 12 12*0 21 42 14*0 21 42 94
  //   13*0 21 42 0 56 12*0 21 42 55 13*0 21 42 84 13*0 21 42 14*0 21 42 14*0 21 42 14*0 21 42 21 52 12*0
  //   21 42 21 22 52 11*0 21 42 21 22 34 11*0 21 42 21 62 12*0 21 42 73 13*0 21 42 57 13*0 21 42 21 12
  //   12*0 21 42 14*0 21 42 21 12 12*0 21 42 94 13*0 21 42 0 56 12*0 21 42 55 13*0 21 42 84 13*0 21 42
  //   14*0 21 42 14*0 21 42 14*0 21 42 21 52 12*0 21 42 21 22 52 11*0 21 42 21 22 34 11*0 21 42 21 62 12*0
  //   21 42 73 13*0 21 42 57 13*0 21 42 21 12 12*0 21 42 21 12 12*0 21 42 21 12 12*0 21 42 94 13*0 21 42 0
  //   56 12*0 21 42 55 13*0 21 42 84 13*0 21 42 14*0 21 42 14*0 21 0 0 84 35 51 5*0 61 4*0 21 0 0 84 35 51
  //   5*0 61 4*0 21 0 0 84 35 51 5*0 61 4*0 21 0 0 84 35 51 5*0 61 4*0 21 0 0 84 35 51 5*0 61 4*0 21 0 0
  //   84 35 51 5*0 61 4*0 21 0 0 84 35 51 5*0 61 4*0 21 0 0 84 35 51 5*0 61 4*0 21 0 0 84 35 51 5*0 61 4*0
  //   21 0 0 84 35 51 5*0 61 4*0 21 0 0 84 35 51 5*0 61 4*0 21 0 0 84 35 51 5*0 61 4*0 21 0 0 84 35 51 5*0
  //   61 4*0 21 0 0 84 35 51 5*0 61 4*0 21 0 0 84 35 51 5*0 61 4*0 21 0 0 84 35 51 5*0 61 4*0 21 0 61 8*0
  //   61 81 21 0 0 21 0 61 8*0 61 81 21 0 0 21 0 61 8*0 61 81 21 0 0 21 0 61 8*0 61 81 21 0 0 21 0 61 8*0
  //   61 81 21 0 0 21 0 61 8*0 61 81 21 0 0 21 0 61 8*0 61 81 21 0 0 21 0 61 8*0 61 81 21 0 0 21 0 61 8*0
  //   61 81 21 0 0 21 0 61 8*0 61 81 21 0 0 21 0 61 8*0 61 81 21 0 0 21 0 61 8*0 61 81 21 0 0 21 0 61 8*0
  //   61 81 21 0 0 21 0 61 8*0 61 81 21 0 0 21 0 61 8*0 61 81 21 0 0 21 0 61 8*0 61 81 21 258*0 21 5*0 21
  //   0 84 35 51 5*0 21 5*0 21 0 84 35 51 5*0 21 5*0 21 0 84 35 51 5*0 21 5*0 21 0 84 35 51 5*0 21 5*0 21
  //   0 84 35 51 5*0 21 5*0 21 0 84 35 51 5*0 21 5*0 21 0 84 35 51 5*0 21 5*0 21 0 84 35 51 5*0 21 5*0 21
  //   0 84 35 51 5*0 21 5*0 21 0 84 35 51 5*0 21 5*0 21 0 84 35 51 5*0 21 5*0 21 0 84 35 51 5*0 21 5*0 21
  //   0 84 35 51 5*0 21 5*0 21 0 84 35 51 5*0 21 5*0 21 0 84 35 51 5*0 21 5*0 21 0 84 35 51
  //   contents of rom_2 (hex, n*v repeats v):
  //   0 2 10 14*0 2 0 2 10 12*0 2 0 2 0 10 11*0 2 0 2 0 10 11*0 2 0 2 10 12*0 2 0 10 13*0 2 0 10 13*0 2 0
  //   0 10 12*0 2 12 14*0 2 12 14*0 2 0 4 10 12*0 2 8 0 10 12*0 2 0 10 13*0 2 0 10 13*0 2 10 14*0 2 11
  //   14*0 2 10 14*0 2 0 2 10 12*0 2 0 2 0 10 11*0 2 0 2 0 10 11*0 2 0 2 10 12*0 2 0 10 13*0 2 0 10 13*0 2
  //   0 0 10 12*0 2 0 0 10 12*0 2 12 14*0 2 0 4 10 12*0 2 8 0 10 12*0 2 0 10 13*0 2 0 10 13*0 2 10 14*0 2
  //   11 14*0 2 10 14*0 2 0 2 10 12*0 2 0 2 0 10 11*0 2 0 2 0 10 11*0 2 0 2 10 12*0 2 0 10 13*0 2 0 10
  //   13*0 2 0 0 10 12*0 2 12 14*0 2 0 0 10 12*0 2 0 4 10 12*0 2 8 0 10 12*0 2 0 10 13*0 2 0 10 13*0 2 10
  //   14*0 2 11 14*0 2 10 14*0 2 0 2 10 12*0 2 0 2 0 10 11*0 2 0 2 0 10 11*0 2 0 2 10 12*0 2 0 10 13*0 2 0
  //   10 13*0 2 0 0 10 12*0 2 0 0 10 12*0 2 0 0 10 12*0 2 0 4 10 12*0 2 8 0 10 12*0 2 0 10 13*0 2 0 10
  //   13*0 2 10 14*0 2 11 14*0 2 4*0 10 10*0 2 4*0 10 10*0 2 4*0 10 10*0 2 4*0 10 10*0 2 4*0 10 10*0 2 4*0
  //   10 10*0 2 4*0 10 10*0 2 4*0 10 10*0 2 4*0 10 10*0 2 4*0 10 10*0 2 4*0 10 10*0 2 4*0 10 10*0 2 4*0 10
  //   10*0 2 4*0 10 10*0 2 4*0 10 10*0 2 4*0 10 10*0 2 12*0 11 0 0 2 12*0 11 0 0 2 12*0 11 0 0 2 12*0 11 0
  //   0 2 12*0 11 0 0 2 12*0 11 0 0 2 12*0 11 0 0 2 12*0 11 0 0 2 12*0 11 0 0 2 12*0 11 0 0 2 12*0 11 0 0
  //   2 12*0 11 0 0 2 12*0 11 0 0 2 12*0 11 0 0 2 12*0 11 0 0 2 12*0 11 258*0 2 5*0 2 9*0 2 5*0 2 9*0 2
  //   5*0 2 9*0 2 5*0 2 9*0 2 5*0 2 9*0 2 5*0 2 9*0 2 5*0 2 9*0 2 5*0 2 9*0 2 5*0 2 9*0 2 5*0 2 9*0 2 5*0
  //   2 9*0 2 5*0 2 9*0 2 5*0 2 9*0 2 5*0 2 9*0 2 5*0 2 9*0 2 5*0 2
  //   Write
  //   Calculation Register
  //   A Register
  //   B Register
  //   OUTPUT
  //   INPUT
endmodule

module ALU (
  input  [7:0] A,
  input  [7:0] B,
  input  [3:0] CAL,
  output Zero,
  output [7:0] C,
  output Overflow
);

  wire n4_bit_alu_1_lsb_2, n4_bit_alu_1_msb_2, n4_bit_alu_1_zero, n4_bit_alu_2_lsb_2, n4_bit_alu_2_zero;

  _4_Bit_ALU u_4_bit_alu_1 (
    .A0(A[0]), .A1(A[1]), .A2(A[2]), .A3(A[3]), .B0(B[0]), .B1(B[1]), .B2(B[2]), .B3(B[3]), .OP0(CAL[0]),
    .OP1(CAL[1]), .OP2(CAL[2]), .OP3(CAL[3]), .Mode(1'b0), .Zero(n4_bit_alu_1_zero), .Q0(C[0]), .Q1(C[1]),
    .Q2(C[2]), .Q3(C[3]), .MSB_2(n4_bit_alu_1_msb_2), .LSB_2(n4_bit_alu_1_lsb_2), .LSB(Overflow),
    .MSB(n4_bit_alu_2_lsb_2));
  _4_Bit_ALU u_4_bit_alu_2 (
    .A0(A[4]), .A1(A[5]), .A2(A[6]), .A3(A[7]), .B0(B[4]), .B1(B[5]), .B2(B[6]), .B3(B[7]), .OP0(CAL[0]),
    .OP1(CAL[1]), .OP2(CAL[2]), .OP3(CAL[3]), .Mode(1'b1), .Zero(n4_bit_alu_2_zero), .Q0(C[4]), .Q1(C[5]),
    .Q2(C[6]), .Q3(C[7]), .MSB_2(Overflow), .LSB_2(n4_bit_alu_2_lsb_2), .LSB(n4_bit_alu_1_msb_2),
    .MSB(n4_bit_alu_1_lsb_2));
  and and_1 (Zero, n4_bit_alu_1_zero, n4_bit_alu_2_zero);
endmodule
